# Fritzing sketch pianoKeyboard (saved by Fritzing 0.9.3b)
breadboards: 1

parts:
  Part1 = Arduino Mega ADK (Rev3)
  LED1 = smd LED [color="Green (570nm)" package="1206 [SMD]"]
  LED2 = smd LED [color="Red (633nm)" package="1206 [SMD]"]
  R1 = Resistor [tolerance=±5% resistance=220 package=THT]
  R2 = Resistor [tolerance=±5% resistance=220 package=THT]
  LED3 = RGB LED (com. cathode, rgb) [package="5 mm [THT]"]
  Keypad4x2 = Keypad Membran 4x4
  R3 = Resistor [tolerance=±5% resistance=220 package=THT]
  R4 = Resistor [tolerance=±5% resistance=220 package=THT]
  R5 = Resistor [tolerance=±5% resistance=220 package=THT]
  J1 = Piezo Speaker

nets:
  N1: Part1.D12_PWM, J1.pin2
  N2: Part1.D9_PWM, Keypad4x2.Pin1
  N3: Part1.D8_PWM, Keypad4x2.Pin2
  N4: Part1.GND, LED1.cathode, LED2.cathode, LED3.common_cathode, J1.pin1
  N5: Part1.D2_PWM, Keypad4x2.Pin8
  N6: Part1.D3_PWM, Keypad4x2.Pin7
  N7: Part1.D4_PWM, Keypad4x2.Pin6
  N8: Part1.D5_PWM, Keypad4x2.Pin5
  N9: Part1.D6_PWM, Keypad4x2.Pin4
  N10: Part1.D7_PWM, Keypad4x2.Pin3
  N11: Part1.D22, R4.Pin_1
  N12: Part1.D23, R5.Pin_1
  N13: Part1.D24, R3.Pin_1
  N14: Part1.D52/SCK, R1.Pin_0
  N15: Part1.D53/SS, R2.Pin_1
  N16: LED1.anode, R1.Pin_1
  N17: LED2.anode, R2.Pin_0
  N18: LED3.red_anode, R4.Pin_0
  N19: LED3.green_anode, R3.Pin_0
  N20: LED3.blue_anode, R5.Pin_0

custom parts:
  Keypad Membran 4x4: Membrane Keypad 4x4 Matrix

// code stored in the sketch: betterPiano.ino
/*
   Expanded Music Keyboard to include more notes
   @author Dustin Mullins
   last updated 8/29/2022
*/
#include <Keypad.h>
#include "pitches.h"
const int MAX_NOTES = 9; // max number of notes allowed for recording

// keypad setup
const byte ROWS = 4; //four rows
const byte COLS = 4; //four columns
//define the cymbols on the buttons of the keypads
char hexaKeys[ROWS][COLS] = {
  {'1', '2', '3', 'A'},
  {'4', '5', '6', 'B'},
  {'7', '8', '9', 'C'},
  {'*', '0', '#', 'D'}
};
byte rowPins[ROWS] = {9, 8, 7, 6}; //connect to the row pinouts of the keypad
byte colPins[COLS] = {5, 4, 3, 2}; //connect to the column pinouts of the keypad

//initialize an instance of class NewKeypad
Keypad customKeypad = Keypad( makeKeymap(hexaKeys), rowPins, colPins, ROWS, COLS);

//LED setup
int redPin = 52;
int greenPin = 53;
int Rpin = 22;
int Gpin = 24;
int Bpin = 23;
int rvalue;
int gvalue;
int bvalue;

// pitches setup
int melody[] = {
  NOTE_C5, NOTE_D5, NOTE_E5, NOTE_F5, NOTE_G5, NOTE_A5, NOTE_B5, NOTE_C6, NOTE_G6, NOTE_A6
}; // 10 different notes - more in pitches .h file
int duration = 500; // duration of notes (500 ms)
int record[MAX_NOTES]; // array used for storing notes in recording
void setup() {
  // put your setup code here, to run once:
  // led output setup
  pinMode(redPin, OUTPUT);
  pinMode(greenPin, OUTPUT);
  pinMode(Rpin, OUTPUT);
  pinMode(Gpin, OUTPUT);
  pinMode(Bpin, OUTPUT);
}

void loop() {
  // put your main code here, to run repeatedly:

  // gets key press from pad
  char customKey = customKeypad.getKey();

  // keys 1-9 play notes in melody[0:8]
  if (customKey == '1') {
    tone(12, melody[0], duration);
    digitalWrite(Rpin, HIGH);
    delay(duration);
    digitalWrite(Rpin, LOW);
  } else if (customKey == '2') {
    tone(12, melody[1], duration);
    digitalWrite(Rpin, HIGH);
    delay(duration);
    digitalWrite(Rpin, LOW);
  } else if (customKey == '3') {
    tone(12, melody[2], duration);
    digitalWrite(Rpin, HIGH);
    digitalWrite(Gpin, HIGH);
    delay(duration);
    digitalWrite(Gpin, LOW);
    digitalWrite(Rpin, LOW);
  } else if (customKey == '4') {
    tone(12, melody[3], duration);
    digitalWrite(Rpin, HIGH);
    digitalWrite(Gpin, HIGH);
    delay(duration);
    digitalWrite(Gpin, LOW);
    digitalWrite(Rpin, LOW);
  } else if (customKey == '5') {
    tone(12, melody[4], duration);
    digitalWrite(Gpin, HIGH);
    delay(duration);
    digitalWrite(Gpin, LOW);
  } else if (customKey == '6') {
    tone(12, melody[5], duration);
    digitalWrite(Bpin, HIGH);
    digitalWrite(Gpin, HIGH);
    delay(duration);
    digitalWrite(Gpin, LOW);
    digitalWrite(Bpin, LOW);
  } else if (customKey == '7') {
    tone(12, melody[6], duration);
    digitalWrite(Bpin, HIGH);
    digitalWrite(Gpin, HIGH);
    delay(duration);
    digitalWrite(Gpin, LOW);
    digitalWrite(Bpin, LOW);
  } else if (customKey == '8') {
    tone(12, melody[7], duration);
    digitalWrite(Bpin, HIGH);
    delay(duration);
    digitalWrite(Bpin, LOW);
  } else if (customKey == '9') {
    tone(12, melody[8], duration);
    digitalWrite(Bpin, HIGH);
    delay(duration);
    digitalWrite(Bpin, LOW);
  }

  if (customKey == 'A') { // Recording button
    int i = 0;
    digitalWrite(redPin, HIGH);
    while (i < MAX_NOTES) { // runs until recording has reached MAX_NOTES number of notes
      customKey = customKeypad.getKey();
      if (customKey == '1') {
        tone(12, melody[0], duration);
        digitalWrite(Rpin, HIGH);
        delay(duration);
        digitalWrite(Rpin, LOW);
        record[i] = 0;
        i++;
      } else if (customKey == '2') {
        tone(12, melody[1], duration);
        digitalWrite(Rpin, HIGH);
        delay(duration);
        digitalWrite(Rpin, LOW);
        record[i] = 1;
        i++;
      } else if (customKey == '3') {
        tone(12, melody[2], duration);
        digitalWrite(Rpin, HIGH);
        digitalWrite(Gpin, HIGH);
        delay(duration);
        digitalWrite(Gpin, LOW);
        digitalWrite(Rpin, LOW);
        record[i] = 2;
        i++;
      } else if (customKey == '4') {
        tone(12, melody[3], duration);
        digitalWrite(Rpin, HIGH);
        digitalWrite(Gpin, HIGH);
        delay(duration);
        digitalWrite(Gpin, LOW);
        digitalWrite(Rpin, LOW);
        record[i] = 3;
        i++;
      } else if (customKey == '5') {
        tone(12, melody[4], duration);
        digitalWrite(Gpin, HIGH);
        delay(duration);
        digitalWrite(Gpin, LOW);
        record[i] = 4;
        i++;
      } else if (customKey == '6') {
        tone(12, melody[5], duration);
        digitalWrite(Bpin, HIGH);
        digitalWrite(Gpin, HIGH);
        delay(duration);
        digitalWrite(Gpin, LOW);
        digitalWrite(Bpin, LOW);
        record[i] = 5;
        i++;
      } else if (customKey == '7') {
        tone(12, melody[6], duration);
        digitalWrite(Bpin, HIGH);
        digitalWrite(Gpin, HIGH);
        delay(duration);
        digitalWrite(Gpin, LOW);
        digitalWrite(Bpin, LOW);
        record[i] = 6;
        i++;
      } else if (customKey == '8') {
        tone(12, melody[7], duration);
        digitalWrite(Bpin, HIGH);
        delay(duration);
        digitalWrite(Bpin, LOW);
        record[i] = 7;
        i++;
      } else if (customKey == '9') {
        tone(12, melody[7], duration);
        digitalWrite(Bpin, HIGH);
        delay(duration);
        digitalWrite(Bpin, LOW);
        record[i] = 8;
        i++;
      }
    }
    digitalWrite(redPin, LOW);
    int note;
    digitalWrite(greenPin, HIGH);
    delay(duration * 2);
    for (int i = 0; i < MAX_NOTES; i++) {
      note = record[i];
      tone(12, melody[note], duration);
      switch (note) {
        case 0:
          digitalWrite(Rpin, HIGH);
          delay(duration);
          digitalWrite(Rpin, LOW);
          break;
        case 1:
          digitalWrite(Rpin, HIGH);
          delay(duration);
          digitalWrite(Rpin, LOW);
          break;
        case 2:
          digitalWrite(Rpin, HIGH);
          digitalWrite(Gpin, HIGH);
          delay(duration);
          digitalWrite(Gpin, LOW);
          digitalWrite(Rpin, LOW);
          break;
        case 3:
          digitalWrite(Rpin, HIGH);
          digitalWrite(Gpin, HIGH);
          delay(duration);
          digitalWrite(Gpin, LOW);
          digitalWrite(Rpin, LOW);
          break;
        case 4:
          digitalWrite(Gpin, HIGH);
          delay(duration);
          digitalWrite(Gpin, LOW);
          break;
        case 5:
          digitalWrite(Bpin, HIGH);
          digitalWrite(Gpin, HIGH);
          delay(duration);
          digitalWrite(Gpin, LOW);
          digitalWrite(Bpin, LOW);
          break;
        case 6:
          digitalWrite(Bpin, HIGH);
          digitalWrite(Gpin, HIGH);
          delay(duration);
          digitalWrite(Gpin, LOW);
          digitalWrite(Bpin, LOW);
          break;
        case 7:
          digitalWrite(Bpin, HIGH);
          delay(duration);
          digitalWrite(Bpin, LOW);
          break;
        case 8:
          digitalWrite(Bpin, HIGH);
          delay(duration);
          digitalWrite(Bpin, LOW);
          break;
        default:
          digitalWrite(Rpin, LOW);
          digitalWrite(Gpin, LOW);
          digitalWrite(Bpin, LOW);
          break;
      }
    }
    digitalWrite(greenPin, LOW);
    digitalWrite(Rpin, LOW);
    digitalWrite(Gpin, LOW);
    digitalWrite(Bpin, LOW);
  }

  if (customKey == 'B') {
    int pNote;
    digitalWrite(greenPin, HIGH);
    delay(duration * 2);
    for (int i = 0; i < MAX_NOTES; i++) {

      pNote = record[i];
      tone(12, melody[pNote], duration);
      switch (pNote) {
        case 0:
          digitalWrite(Rpin, HIGH);
          delay(duration);
          digitalWrite(Rpin, LOW);
          break;
        case 1:
          digitalWrite(Rpin, HIGH);
          delay(duration);
          digitalWrite(Rpin, LOW);
          break;
        case 2:
          digitalWrite(Rpin, HIGH);
          digitalWrite(Gpin, HIGH);
          delay(duration);
          digitalWrite(Gpin, LOW);
          digitalWrite(Rpin, LOW);
          break;
        case 3:
          digitalWrite(Rpin, HIGH);
          digitalWrite(Gpin, HIGH);
          delay(duration);
          digitalWrite(Gpin, LOW);
          digitalWrite(Rpin, LOW);
          break;
        case 4:
          digitalWrite(Gpin, HIGH);
          delay(duration);
          digitalWrite(Gpin, LOW);
          break;
        case 5:
          digitalWrite(Bpin, HIGH);
          digitalWrite(Gpin, HIGH);
          delay(duration);
          digitalWrite(Gpin, LOW);
          digitalWrite(Bpin, LOW);
          break;
        case 6:
          digitalWrite(Bpin, HIGH);
          digitalWrite(Gpin, HIGH);
          delay(duration);
          digitalWrite(Gpin, LOW);
          digitalWrite(Bpin, LOW);
          break;
        case 7:
          digitalWrite(Bpin, HIGH);
          delay(duration);
          digitalWrite(Bpin, LOW);
          break;
        case 8:
          digitalWrite(Bpin, HIGH);
          delay(duration);
          digitalWrite(Bpin, LOW);
          break;
        default:
          digitalWrite(Rpin, LOW);
          digitalWrite(Gpin, LOW);
          digitalWrite(Bpin, LOW);
          break;
      }
    }
    digitalWrite(greenPin, LOW);
  }
}
